# Fritzing sketch Rancang Bangun alat pendeteksi api dan kebocoran gas (saved by Fritzing 0.9.9b)
breadboards: 1

parts:
  LED1 = LED - 5mm [color="Green (565nm)" package="5 mm [THT]"]
  LED3 = LED - 5mm [color="Red (633nm)" package="5 mm [THT]"]
  R3 = Resistor [tolerance=±5% resistance=220 package=THT]
  U1 = GAS_SENSOR [package=mq-3]  # not connected
  Mod1 = KY-026 Flame Sensor Module [package="Breakout board"]  # not connected
  J1 = Piezo Speaker
  U2 = ESP32-38PinWide [part_number=ESP32-38PinWide]
  R2 = Resistor [tolerance=±5% resistance=220 package=THT]

nets:
  N1: LED1.cathode, U2.GPIO17
  N2: LED1.anode, R2.Pin_0
  N3: LED3.cathode, U2.GPIO16
  N4: LED3.anode, R3.Pin_0
  N5: R3.Pin_1, J1.pin1, U2.GPIO11, R2.Pin_1

custom parts:
  KY-026 Flame Sensor Module: KY-026 Flame Sensor Module reacts in the presence of fire.
  ESP32-38PinWide: Generic 38-Pin ESP32 with wide format (only access to one side of pins on a breadboard) based on Stephen Lilley's HiLetgo ESP-WROOM-32 ESP32 ESP-32S Development Board.
